# Fritzing sketch Esquema-Final-A (saved by Fritzing 0.8.5b)
breadboards: 2

parts:
  U1 = LCD-16X2 [package=lcd-16x2]
  T1 = LM35 Temperature Sensor [package="TO92 [THT]"]
  SET_PONIT = Momentary Switch [package=ksa_sealed_tac_switch]
  DHT11 = Header 3 [package=screwterminal-3.5mm-3_lock.007s]
  GPS = Header 4 [package=jst-4-pth]
  R1 = Resistor [tolerance=±5% resistance=10k package=THT]
  1K = POT [package=pot_alpha_rv16af-20]
  Parte1 = Arduino Mega ADK (Rev3)
  Humedad_Suelo = Header 4 [package=jst-4-pth]
  RTC = Header 5x2 [package=2x5-ra]
  UVSensor = Header 5x2 [package=2x5-ra]

nets:
  GND: U1.VSS, U1.R_W, U1.K, T1.GND, SET_PONIT.3, SET_PONIT.4, DHT11.3, GPS.4, R1.Pin_1, 1K.A, Parte1.GND, Humedad_Suelo.2, RTC.8, UVSensor.6
  VDD: U1.VDD, U1.A, T1.+Vs, DHT11.1, GPS.1, 1K.E, Parte1.5V, Humedad_Suelo.1, RTC.10
  N1: U1.VO, 1K.S
  N2: U1.RS, Parte1.D12_PWM
  N3: U1.E, Parte1.D11_PWM
  N4: U1.DB4, Parte1.D10_PWM
  N5: U1.DB5, Parte1.D9_PWM
  N6: U1.DB6, Parte1.D8_PWM
  N7: U1.DB7, Parte1.D7_PWM
  N8: T1.Vout, Parte1.A7
  N9: SET_PONIT.1, SET_PONIT.2, R1.Pin_0, Parte1.D2_PWM
  N10: DHT11.2, Parte1.D6_PWM
  N11: GPS.2, Parte1.D31
  N12: GPS.3, Parte1.D13_PWM
  N13: Parte1.A0, UVSensor.4
  N14: Parte1.A1, UVSensor.8
  N15: Parte1.A2, Humedad_Suelo.4
  N16: Parte1.D21/SCL, RTC.6
  N17: Parte1.D20/SDA, RTC.4
  N18: Parte1.D19/RX1, RTC.2
  N19: Parte1.3V3, UVSensor.2, UVSensor.10
