# Fritzing sketch Esquema-Final-B (saved by Fritzing 0.8.5b)

parts:
  Parte1 = Arduino Mega ADK (Rev3)
  Keyboard = Header 8 [package=1x08_smd]
  R1 = Resistor [tolerance=±5% resistance=1k package=THT]
  R2 = Resistor [tolerance=±5% resistance=1k package=THT]
  R3 = Resistor [tolerance=±5% resistance=1k package=THT]
  R4 = Resistor [tolerance=±5% resistance=1k package=THT]
  GSM/GPRS = Header 12 [package=1x12_machine-pin-header_lock.004]
  LED1 = LED - 5mm [color="Red (633nm)" package="5 mm [THT]"]
  R5 = Resistor [tolerance=±5% resistance=220 package=THT]

nets:
  N1: Parte1.D17/RX2, GSM/GPRS.4
  N2: Parte1.D16/TX2, GSM/GPRS.3
  N3: Parte1.5V, R4.Pin_1, GSM/GPRS.1
  N4: Parte1.GND, GSM/GPRS.6, GSM/GPRS.11, R5.Pin_1
  N5: Parte1.D5_PWM, LED1.anode
  N6: Parte1.D39, R1.Pin_0
  N7: Parte1.D41, R2.Pin_0
  N8: Parte1.D43, R3.Pin_0
  N9: Parte1.D45, R4.Pin_0
  N10: Parte1.D47, Keyboard.4
  N11: Parte1.D49, Keyboard.3
  N12: Parte1.D51/MOSI, Keyboard.2
  N13: Parte1.D53/SS, Keyboard.1
